# Fritzing sketch schematic (saved by Fritzing 0.9.3b)

parts:
  WeMos_D1_Mini1 = WeMos D1 Mini
  U1 = SWITCH-SPST-2 [package=r_sw_th]
  R1 = Resistor [tolerance=±5% resistance=2.2k package="2512 [SMD]"]
  R2 = Resistor [tolerance=±5% resistance=10k package="2512 [SMD]"]
  VCC2 = Battery block 9V
  M2 = DC Motor
  M3 = BTS7960
  U2 = Voltage Regulator - 5V [package="TO220 [THT]"]
  M4 = BTS7960
  M5 = DC Motor

nets:
  N1: WeMos_D1_Mini1.5V, M3.pin7, U2.output_voltage, M4.pin7
  N2: WeMos_D1_Mini1.A0, R1.Pin_0, R2.Pin_1
  N3: WeMos_D1_Mini1.D1, M3.pin3, M3.pin4
  N4: WeMos_D1_Mini1.D2, M3.pin2
  N5: WeMos_D1_Mini1.D3, M3.pin1
  N6: WeMos_D1_Mini1.D5, M4.pin3, M4.pin4
  N7: WeMos_D1_Mini1.D6, M4.pin2
  N8: WeMos_D1_Mini1.D7, M4.pin1
  N9: WeMos_D1_Mini1.G, M3.pin12, U2.GND, M4.pin8, M4.pin11
  N10: U1.O, VCC2.+
  N11: U1.P, R2.Pin_0, M3.pin11, U2.input_voltage, M4.pin12
  N12: R1.Pin_1, VCC2.-
  N13: M2.pin_1, M3.pin10
  N14: M2.pin_2, M3.pin9
  N15: M4.pin9, M5.pin_2
  N16: M4.pin10, M5.pin_1

notes:
  12V batteries in parallel...

custom parts:
  BTS7960: BTS7960 43A Peak Power H-Bridge PWM Motor Driver
